# Fritzing sketch components (saved by Fritzing 0.9.6b)
breadboards: 1

parts:
  Mod1 = Raspberry Pi 4B
  PIR1 = PIR sensor
  RCWL-0516_Microwave_Radar_Motion_Sensor1 = RCWL-0516 Microwave Radar Motion Sensor Module
  GY1 = MPU-6050 Board GY-521 [form="♀ (female)" package=THT]
  Part1 = ACS712 Low Current Sensor Board v12
  S2 = Toggle Switch [package=THT]

nets:
  N1: Mod1.3V3, GY1.pin1
  N2: Mod1.GPIO2, GY1.pin4
  N3: Mod1.GPIO3, GY1.pin3
  GND: Mod1.GND, PIR1.GND, RCWL-0516_Microwave_Radar_Motion_Sensor1.GND, GY1.pin2, Part1.GND, S2.COM
  N4: Mod1.GPIO17, RCWL-0516_Microwave_Radar_Motion_Sensor1.OUT
  N5: Mod1.GPIO22, PIR1.SIG
  N6: Mod1.GPIO26, S2.L2
  N7: Mod1.RUN, S2.L1
  VDD: PIR1.VDD, RCWL-0516_Microwave_Radar_Motion_Sensor1.VIN, Part1.IP+, Part1.IP-, Part1.5V

notes:
  power

custom parts:
  RCWL-0516 Microwave Radar Motion Sensor Module: The RCWL-0516 is a microwave radar motion sensor module. Input voltage is 4V to 28V. The 3V3 pin is a power output.
  MPU-6050 Board GY-521: Acelerometro y Giroscopio MPU-6050 Board GY-521
